// Logisim project B2_G1.circ as structural Verilog: 4 circuits, main circuit Memory
module Control (
  input  [3:0] Opcode,
  output Bneq,
  output RegDst,
  output Jump,
  output Branch,
  output MemRead,
  output MemtoReg,
  output [3:0] ALUop,
  output MemWrite,
  output ALUSrc,
  output RegWrite,
  output Shift
);

  wire [15:14] rom_1_data;

  ROM #(.addrWidth(4), .dataWidth(16)) rom_1 (
    .addr(Opcode),
    .data({rom_1_data, Bneq, RegDst, Jump, Branch, MemRead, MemtoReg, ALUop, MemWrite, ALUSrc, RegWrite, Shift}));  // open: sel

  // Notes on the sheet:
  //   contents of rom_1 (hex, n*v repeats v):
  //   1022 1002 16 10c2 6 1062 1083 1093 2c 2460 66 460 800 26 326 1012
endmodule

module Memory (
  input  [7:0] Address,
  input  [7:0] WriteData,
  input  Enable,
  input  CLK,
  input  MemWrite,
  input  MemRead,
  output [7:0] ReadData
);

  RAM #(.bus("separate")) ram_1 (
    .addr(Address), .din(WriteData), .data(ReadData), .str(MemWrite), .sel(Enable), .clk(CLK), .ld(MemRead),
    .clr(1'b0));
endmodule

module Main (
);

  wire and_1_out, and_2_out, clock_1_out, comparator_1_eq, control_1_alusrc, control_1_bneq,
       control_1_branch, control_1_jump, control_1_memread, control_1_memtoreg, control_1_memwrite,
       control_1_regdst, control_1_regwrite, control_1_shift, mips_alu_1_p4, multiplexer_4_out, not_1_out,
       not_2_out, not_3_out, subtractor_1_bout;
  wire [3:0] control_1_aluop, multiplexer_1_out, rom_1_data_3;
  wire [7:0] adder_1_out, adder_2_out, bit_extender_1_out, Data_Memory_readdata, mips_alu_1_p5,
       multiplexer_2_out, multiplexer_3_out, multiplexer_5_out, multiplexer_6_out, multiplexer_7_out,
       multiplexer_8_out, PC_q, Register_read_data_1, Register_read_data_2, rom_1_data, Stack_Memory_readdata;
  wire [15:8] rom_1_data_2;
  wire [31:0] bit_extender_2_out, mips_alu_1_p2;
  wire [31:8] mips_alu_1_p5_2;

  Clock clock_1 (.out(clock_1_out));
  Register_part PC (.D(multiplexer_6_out), .en(1'b1), .Q(PC_q), .clk(clock_1_out), .clr(1'b0));
  ROM #(.dataWidth(20)) rom_1 (.addr(PC_q), .data({rom_1_data_3, rom_1_data_2, rom_1_data}));  // open: sel
  Adder adder_1 (.a(PC_q), .b(8'h1), .out(adder_1_out));  // open: cin, cout
  Multiplexer #(.width(4), .enable("false")) multiplexer_1 (
    .in0(rom_1_data_2[11:8]), .in1(rom_1_data[7:4]), .out(multiplexer_1_out), .sel(control_1_regdst));
  Register Register (
    .Read_Register_1(rom_1_data_2[15:12]), .Read_Register_2(rom_1_data_2[11:8]),
    .Write_Register(multiplexer_1_out), .Write_Data(multiplexer_8_out), .Register_Write(control_1_regwrite),
    .CLK(clock_1_out), .Read_Data_1(Register_read_data_1), .Read_Data_2(Register_read_data_2));
  Comparator #(.width(4)) comparator_1 (.a(rom_1_data_2[15:12]), .b(4'b0110), .eq(comparator_1_eq));  // open: gt, lt
  assign bit_extender_1_out = {{4{1'b0}}, rom_1_data[3:0]};  // Bit_Extender bit_extender_1
  Control control_1 (
    .Opcode(rom_1_data_3), .Bneq(control_1_bneq), .RegDst(control_1_regdst), .Jump(control_1_jump),
    .Branch(control_1_branch), .MemRead(control_1_memread), .MemtoReg(control_1_memtoreg),
    .ALUop(control_1_aluop), .MemWrite(control_1_memwrite), .ALUSrc(control_1_alusrc),
    .RegWrite(control_1_regwrite), .Shift(control_1_shift));
  Multiplexer #(.width(8), .enable("false")) multiplexer_2 (
    .in0(Register_read_data_1), .in1(bit_extender_1_out), .out(multiplexer_2_out), .sel(control_1_shift));
  Multiplexer #(.width(8), .enable("false")) multiplexer_3 (
    .in0(Register_read_data_2), .in1(rom_1_data), .out(multiplexer_3_out), .sel(control_1_alusrc));
  Adder adder_2 (.a(adder_1_out), .b(rom_1_data), .out(adder_2_out));  // open: cin, cout
  assign bit_extender_2_out = {{24{multiplexer_2_out[7]}}, multiplexer_2_out};  // Bit_Extender bit_extender_2
  // MIPS_ALU mips_alu_1: pin names not known; wires that end beside it: bit_extender_2_out, mips_alu_1_p2, control_1_aluop, mips_alu_1_p4, {mips_alu_1_p5_2, mips_alu_1_p5}
  assign mips_alu_1_p2 = {{24{multiplexer_3_out[7]}}, multiplexer_3_out};  // Bit_Extender bit_extender_3
  not not_1 (not_1_out, mips_alu_1_p4);
  Multiplexer #(.enable("false")) multiplexer_4 (
    .in0(mips_alu_1_p4), .in1(not_1_out), .out(multiplexer_4_out), .sel(control_1_bneq));
  Subtractor subtractor_1 (.a(mips_alu_1_p5), .b(Register_read_data_1), .bout(subtractor_1_bout));  // open: out, bin
  Multiplexer #(.width(8), .enable("false")) multiplexer_5 (
    .in0(adder_1_out), .in1(adder_2_out), .out(multiplexer_5_out), .sel(and_1_out));
  and and_1 (and_1_out, multiplexer_4_out, control_1_branch);
  not not_2 (not_2_out, comparator_1_eq);
  not not_3 (not_3_out, subtractor_1_bout);
  Multiplexer #(.width(8), .enable("false")) multiplexer_6 (
    .in0(multiplexer_5_out), .in1(rom_1_data_2), .out(multiplexer_6_out), .sel(control_1_jump));
  Memory Data_Memory (
    .Address(mips_alu_1_p5), .WriteData(Register_read_data_2), .MemWrite(control_1_memwrite),
    .Enable(not_2_out), .CLK(clock_1_out), .MemRead(control_1_memread), .ReadData(Data_Memory_readdata));
  Memory Stack_Memory (
    .Address(mips_alu_1_p5), .WriteData(Register_read_data_2), .MemWrite(control_1_memwrite),
    .Enable(and_2_out), .CLK(clock_1_out), .MemRead(control_1_memread), .ReadData(Stack_Memory_readdata));
  and and_2 (and_2_out, comparator_1_eq, not_3_out);
  Multiplexer #(.width(8), .enable("false")) multiplexer_7 (
    .in0(Data_Memory_readdata), .in1(Stack_Memory_readdata), .out(multiplexer_7_out), .sel(comparator_1_eq));
  Multiplexer #(.width(8), .enable("false")) multiplexer_8 (
    .in0(mips_alu_1_p5), .in1(multiplexer_7_out), .out(multiplexer_8_out), .sel(control_1_memtoreg));

  // Notes on the sheet:
  //   contents of rom_1 (hex, n*v repeats v):
  //   d66ff d0105 120 91201 c0500 c0000 60112 70112 b1201 c0000 f1230 23300 433ff 11230 a3305 52330 93001
  //   c0000 81264 e1364 b3201 c0000 31110 12130 d0578 d0488 86500 d66ff 86400 d66ff e6201 e6302 b22e0
endmodule

module Register (
  input  Register_Write,
  input  [3:0] Read_Register_1,
  input  [3:0] Read_Register_2,
  input  [3:0] Write_Register,
  input  CLK,
  input  [7:0] Write_Data,
  output [7:0] Read_Data_1,
  output [7:0] Read_Data_2
);

  wire A0_out, A1_out, A2_out, A3_out, A4_out, A5_out, A6_out, decoder_1_out0, decoder_1_out1,
       decoder_1_out2, decoder_1_out3, decoder_1_out4, decoder_1_out5, decoder_1_out6;
  wire [7:0] R0_q, R1_q, R2_q, R3_q, R4_q, R5_q, R6_q;

  Decoder #(.select(3)) decoder_1 (
    .out0(decoder_1_out0), .out1(decoder_1_out1), .out2(decoder_1_out2), .out3(decoder_1_out3),
    .out4(decoder_1_out4), .out5(decoder_1_out5), .out6(decoder_1_out6), .sel(Write_Register[2:0]), .en(1'b1));  // open: out7
  and A0 (A0_out, decoder_1_out0, Register_Write);
  and A1 (A1_out, decoder_1_out1, Register_Write);
  and A2 (A2_out, decoder_1_out2, Register_Write);
  and A3 (A3_out, decoder_1_out3, Register_Write);
  and A4 (A4_out, decoder_1_out4, Register_Write);
  and A5 (A5_out, decoder_1_out5, Register_Write);
  and A6 (A6_out, decoder_1_out6, Register_Write);
  Register_part R0 (.D({8{1'b0}}), .en(A0_out), .Q(R0_q), .clk(CLK), .clr(1'b0));
  Register_part R1 (.D(Write_Data), .en(A1_out), .Q(R1_q), .clk(CLK), .clr(1'b0));
  Register_part R2 (.D(Write_Data), .en(A2_out), .Q(R2_q), .clk(CLK), .clr(1'b0));
  Register_part R3 (.D(Write_Data), .en(A3_out), .Q(R3_q), .clk(CLK), .clr(1'b0));
  Register_part R4 (.D(Write_Data), .en(A4_out), .Q(R4_q), .clk(CLK), .clr(1'b0));
  Register_part R5 (.D(Write_Data), .en(A5_out), .Q(R5_q), .clk(CLK), .clr(1'b0));
  Register_part R6 (.D(Write_Data), .en(A6_out), .Q(R6_q), .clk(CLK), .clr(1'b0));
  Multiplexer #(.select(3), .width(8)) multiplexer_1 (
    .in0(R0_q), .in1(R1_q), .in2(R2_q), .in3(R3_q), .in4(R4_q), .in5(R5_q), .in6(R6_q), .out(Read_Data_1),
    .sel(Read_Register_1[2:0]), .en(1'b1));  // open: in7
  Multiplexer #(.select(3), .width(8)) multiplexer_2 (
    .in0(R0_q), .in1(R1_q), .in2(R2_q), .in3(R3_q), .in4(R4_q), .in5(R5_q), .in6(R6_q), .out(Read_Data_2),
    .sel(Read_Register_2[2:0]), .en(1'b1));  // open: in7
endmodule
